// Logisim project part2.circ as structural Verilog: 1 circuit, main circuit main
module main (
  input  MuxCSel,
  input  in_2,
  input  [3:0] FunSel,
  input  [1:0] OutASel,
  input  [1:0] OutBSel,
  input  [1:0] FunSel_2,
  input  [3:0] RegSel,
  input  [1:0] MuxASel,
  input  [1:0] MuxBSel,
  input  in_10,
  input  in_11,
  input  in_12,
  input  in_13,
  input  [1:0] OutCSel,
  input  [1:0] OutDSel,
  input  [1:0] FunSel_3,
  input  [3:0] RegSel_2,
  input  L_H,
  input  Enable,
  input  [1:0] FunSel_4,
  output [7:0] out_21,
  output [3:0] out_22
);

  wire n4_register_bank_1_p7;
  wire [3:0] main_2_p6;
  wire [7:0] main_1_p1, main_1_p6, multiplexer_1_out, multiplexer_2_out, multiplexer_3_out,
       n3_register_bank_1_p7, n3_register_bank_1_p8, n4_register_bank_1_p8;
  wire [15:8] main_1_p6_2;

  Multiplexer #(.select(2), .width(8), .enable("false")) multiplexer_1 (
    .in0(main_1_p6), .in1(main_1_p1), .in2(n3_register_bank_1_p7), .in3(out_21), .out(multiplexer_1_out),
    .sel(MuxASel));
  // _4_register_bank 4_register_bank_1: pin names not known; wires that end beside it: RegSel, multiplexer_1_out, FunSel_2, OutASel, in_2, OutBSel, n4_register_bank_1_p7, n4_register_bank_1_p8
  Multiplexer #(.select(2), .width(8), .enable("false")) multiplexer_2 (
    .in1(main_1_p6), .in2(main_1_p1), .in3(out_21), .out(multiplexer_2_out), .sel(MuxBSel));  // open: in0
  // _2c_main main_1: pin names not known; wires that end beside it: main_1_p1, L_H, FunSel_4, in_2, Enable, {main_1_p6_2, main_1_p6}
  Multiplexer #(.width(8), .enable("false")) multiplexer_3 (
    .in0(multiplexer_1_out), .in1(n4_register_bank_1_p8), .out(multiplexer_3_out), .sel(MuxCSel));
  // alu2_main main_2: pin names not known; wires that end beside it: multiplexer_3_out, n4_register_bank_1_p7, FunSel, out_22[2], out_21, main_2_p6
  // _3_register_bank 3_register_bank_1: pin names not known; wires that end beside it: RegSel_2, multiplexer_2_out, FunSel_3, OutCSel, in_2, OutDSel, n3_register_bank_1_p7, n3_register_bank_1_p8
  Register #(.width(4)) register_1 (.D(main_2_p6), .en(1'b1), .Q(out_22), .clk(in_2));  // open: clr
  RAM #(.bus("separate")) ram_1 (
    .addr(n3_register_bank_1_p8), .din(out_21), .data(main_1_p1), .str(in_10), .sel(in_11), .clk(in_2),
    .ld(in_12), .clr(in_13));

  // Notes on the sheet:
  //   A
  //   B
  //   C
endmodule
